# Fritzing sketch keep.v4 (saved by Fritzing 1.0.2b)
circuit board: 8.78644cm x 6.22578cm
breadboards: 1

parts:
  100Klfo = Rotary Potentiometer (Small) [maximum_resistance=100kΩ knob_status=50% power=0.5W package=THT]
  100Km2 = Rotary Potentiometer (Small) [maximum_resistance=100kΩ knob_status=50% power=0.5W package=THT]
  100Kx2 = Rotary Potentiometer (Small) [maximum_resistance=100kΩ knob_status=50% power=0.5W package=THT]
  4040 = CD4040E [package="DIP16 [THT]"]
  XR = XR2206 [package=dil16]
  100Kosc = Rotary Potentiometer (Small) [maximum_resistance=100kΩ knob_status=50% power=0.5W package=THT]
  1uf = Electrolytic Capacitor [capacitance=1µF voltage=16V package="100 mil [THT, electrolytic]"]
  100Km1 = Rotary Potentiometer (Small) [maximum_resistance=100kΩ knob_status=50% power=0.5W package=THT]
  Jm2 = female pin header, 3 pins [form="♀ (female)"]
  j40 = female pin header, 6 pins [form="♀ (female)"]
  4_7k = Resistor [tolerance=±5% resistance=4.7k power=0.25W package=THT]
  Jx1 = female pin header, 2 pins [form="♀ (female)"]
  Jxs = female pin header, 2 pins [form="♀ (female)"]
  100k = Resistor [tolerance=±5% resistance=100k power=0.25W package=THT]
  Jx2 = female pin header, 2 pins [form="♀ (female)"]
  1uf_2 = Electrolytic Capacitor [capacitance=1µF voltage=16V package="100 mil [THT, electrolytic]"]
  4_7k_2 = Resistor [tolerance=±5% resistance=4.7k power=0.25W package=THT]
  68nf = Ceramic Capacitor [capacitance=68nF voltage=16V package="200 mil [THT, multilayer]"]
  330o = Resistor [tolerance=±5% resistance=330 power=0.25W package=THT]
  LED3 = LED - 3mm [color="White (8000K)" current=0.030A package="3 mm [THT]"]
  jlfo = female pin header, 2 pins [form="♀ (female)"]
  10Kflt = Rotary Potentiometer (Small) [maximum_resistance=10kΩ knob_status=50% power=0.5W package=THT]
  1uf_3 = Electrolytic Capacitor [capacitance=1µF voltage=16V package="100 mil [THT, electrolytic]"]
  220o = Resistor [tolerance=±5% resistance=220 power=0.25W package=THT]
  J1 = female pin header, 5 pins [form="♀ (female)"]
  J2 = female pin header, 5 pins [form="♀ (female)"]
  Josc = female pin header, 3 pins [form="♀ (female)"]
  VCC1 = Battery
  Jm1 = female pin header, 3 pins [form="♀ (female)"]
  LED2 = LED - 3mm [color="White (8000K)" current=0.030A package="3 mm [THT]"]
  100Kx1 = Rotary Potentiometer (Small) [maximum_resistance=100kΩ knob_status=50% power=0.5W package=THT]
  4_7k_3 = Resistor [tolerance=±1% resistance=4.7k power=0.25W package=THT]
  4_7k_4 = Resistor [tolerance=±1% resistance=4.7k power=0.25W package=THT]
  j40_2 = female pin header, 2 pins [form="♀ (female)"]
  10uf = Electrolytic Capacitor [capacitance=10μF voltage=16V package="100 mil [THT, electrolytic]"]
  Jx3 = female pin header, 2 pins [form="♀ (female)"]
  100Kmx = Rotary Potentiometer (Small) [maximum_resistance=100kΩ knob_status=50% power=0.5W package=THT]
  out = Piezo Speaker
  100n = Ceramic Capacitor [capacitance="100 nF" voltage=35V package="100 mil [THT, multilayer]"]
  4_7k_5 = Resistor [tolerance=±5% resistance=4.7k power=0.25W package=THT]
  4_7k_6 = Resistor [tolerance=±5% resistance=4.7k power=0.25W package=THT]
  10shape = Rotary Potentiometer (Small) [maximum_resistance=10kΩ knob_status=50% power=0.5W package=THT]
  4_7k3 = Resistor [tolerance=±5% resistance=4.7k power=0.25W package=THT]
  Jamp = female pin header, 2 pins [form="♀ (female)"]
  47nf = Ceramic Capacitor [capacitance=47nF voltage=16V package="200 mil [THT, multilayer]"]
  LDR = Photocell (LDR) [power=0.25W dark_resistance_@0.01lx=300kΩ light_resistance_@100lx=400Ω luminance=10lx package=THT]
  40106 = IC, DIP package, 14 pins [chip_label=40106]
  Jled = female pin header, 3 pins [form="♀ (female)"]

nets:
  N1: 100Klfo.wiper, 10uf.+, 40106.pin11
  N2: 100Klfo.leg2, 4040.Input_signal, 330o.Pin_0, 40106.pin10
  N3: 100Km2.leg1, 4040.Q7, Jm2.pin3, j40.pin5
  N4: 100Km2.wiper, Jm2.pin2
  N5: 100Km2.leg2, 4040.Q6, Jm2.pin1, j40.pin3
  N6: 100Kx2.leg1, Jx2.pin1, Jx2.pin2
  N7: 100Kx2.wiper, 4_7k.Pin_1
  VSS: 100Kx2.leg2, 4040.Vss, 4040.Reset, XR.GND, 1uf.-, LED3.cathode, 1uf_3.-, VCC1.-, 100Kx1.leg2, 4_7k_3.Pin_0, 10uf.-, Jx3.pin1, out.pin1, 100n.0, 4_7k_5.Pin_0, 10shape.wiper, 47nf.0, 40106.pin7
  N8: 4040.Q13, j40.pin1
  N9: 4040.Q14, j40.pin2
  N10: 4040.Q5, 100Km1.leg2, j40.pin4, Jm1.pin1
  N11: 4040.Q4, j40.pin6
  N12: 4040.Q1, 100Km1.leg1, Jm1.pin3, LED2.anode, j40_2.pin1, j40_2.pin2
  VDD: 4040.Vdd, XR.VCC, VCC1.+, 4_7k_4.Pin_0, Jx3.pin2, 40106.pin14
  N13: XR.AMSI, 4_7k_6.Pin_0
  N14: XR.STO, 1uf_2.-
  N15: XR.MO, 4_7k3.Pin_1
  N16: XR.TC1, 68nf.0
  N17: XR.TC2, 68nf.1
  N18: XR.TR1, 4_7k_2.Pin_0
  N19: XR.TR2, 4_7k.Pin_0
  N20: XR.FSKI, Jxs.pin1, Jxs.pin2
  N21: XR.WAVEA1, 220o.Pin_1
  N22: XR.WAVEA2, 220o.Pin_0
  N23: XR.SYMA1, 10shape.leg2
  N24: XR.SYMA2, 10shape.leg1
  N25: 100Kosc.wiper, 1uf.+, 100k.Pin_0, 40106.pin9
  N26: 100Kosc.leg2, LDR.pin_0, 40106.pin8
  N27: 100Km1.wiper, Jm1.pin2
  N28: Jx1.pin1, Jx1.pin2, 100Kx1.leg1
  N29: 100k.Pin_1, Josc.pin1, Josc.pin2, Josc.pin3
  N30: 1uf_2.+, 100Kmx.leg1
  N31: 4_7k_2.Pin_1, 100Kx1.wiper
  N32: 330o.Pin_1, jlfo.pin1, jlfo.pin2
  N33: LED3.anode, Jled.pin1, Jled.pin2, Jled.pin3
  N34: 10Kflt.leg1, 1uf_3.+
  N35: 10Kflt.wiper, LDR.pin_1
  N36: 10Kflt.leg2, 100Kmx.leg2, 47nf.1
  N37: J1.pin1, J1.pin2, J1.pin3, J1.pin4, J1.pin5
  N38: J2.pin1, J2.pin2, J2.pin3, J2.pin4, J2.pin5
  N39: LED2.cathode, 4_7k_5.Pin_1
  N40: 4_7k_3.Pin_1, 4_7k_4.Pin_1, 4_7k3.Pin_0
  N41: 100Kmx.wiper, out.pin2, 100n.1
  N42: 4_7k_6.Pin_1, Jamp.pin1, Jamp.pin2

notes:
  keep v.3

custom parts:
  CD4040E: CD4020B, CD4024B, and CD4040B are ripple-carry binary counters. All counter stages are master-slave flip-flops. The state of a counter advances one count on the negative transition of each input pulse; a high level on the RESET line resets the counter to its all zeros state. Schmitt trigger action on the input-pulse line permits unlimited rise and fall times. All inputs and outputs are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
