# Fritzing sketch moat-shark (saved by Fritzing 1.0.3b)
circuit board: 4.99999cm x 10cm
breadboards: 2

parts:
  100Kfm2 = Rotary Potentiometer (Small) [maximum_resistance=100kΩ knob_status=50% power=0.5W package=THT]
  4040A = CD4040E [package="DIP16 [THT]"]
  XR2206 = XR2206 [package=dil16]
  100K = Rotary Potentiometer (Small) [maximum_resistance=100kΩ knob_status=50% power=0.5W package=THT]
  j40 = female pin header, 6 pins [form="♀ (female)"]
  4_7k = Resistor [tolerance=±5% resistance=4.7k power=0.25W package=THT]
  A/B = female pin header, 2 pins [form="♀ (female)"]
  1uf = Electrolytic Capacitor [capacitance=1µF voltage=16V package="100 mil [THT, electrolytic]"]
  4_7k_2 = Resistor [tolerance=±5% resistance=4.7k power=0.25W package=THT]
  68nf = Ceramic Capacitor [capacitance=68nF voltage=16V package="200 mil [THT, multilayer]"]
  220 = Resistor [tolerance=±5% resistance=220 power=0.25W package=THT]
  100Kfm1 = Rotary Potentiometer (Small) [maximum_resistance=100kΩ knob_status=50% power=0.5W package=THT]
  4_7k_3 = Resistor [tolerance=±1% resistance=4.7k power=0.25W package=THT]
  4_7k_4 = Resistor [tolerance=±1% resistance=4.7k power=0.25W package=THT]
  100Kamp = Rotary Potentiometer (Small) [maximum_resistance=100kΩ knob_status=50% power=0.5W package=THT]
  1kshape = Rotary Potentiometer (Small) [maximum_resistance=1kΩ knob_status=50% power=0.5W package=THT]
  4_7k3 = Resistor [tolerance=±5% resistance=4.7k power=0.25W package=THT]
  TRS1 = Audio Jack (TRS) 3.5mm [package="PG203J [THT]"]
  Power_plug1 = Power plug
  out = female pin header, 2 pins [form="♀ (female)"]
  100K_2 = Rotary Potentiometer (Small) [maximum_resistance=100kΩ knob_status=50% power=0.5W package=THT]
  LM324 = LM124-324 Quad Opamp [package="DIP (Dual Inline)"]
  100K_3 = Resistor [tolerance=±5% resistance=100k power=0.25W package=THT]
  1K = Resistor [tolerance=±5% resistance=1k power=0.25W package=THT]
  100K_4 = Resistor [tolerance=±5% resistance=100k power=0.25W package=THT]
  1K_2 = Resistor [tolerance=±5% resistance=1k power=0.25W package=THT]
  100K_5 = Resistor [tolerance=±5% resistance=100k power=0.25W package=THT]
  1K_3 = Resistor [tolerance=±5% resistance=1k power=0.25W package=THT]
  Jamp5 = female pin header, 1 pin [form="♀ (female)"]
  Jamp4 = female pin header, 1 pin [form="♀ (female)"]
  Jamp1 = female pin header, 1 pin [form="♀ (female)"]
  Jamp2 = female pin header, 2 pins [form="♀ (female)"]
  Jamp3 = female pin header, 2 pins [form="♀ (female)"]
  Jamp6 = female pin header, 2 pins [form="♀ (female)"]
  47u = Electrolytic Capacitor [capacitance=47µF voltage=35V package="100 mil [THT, electrolytic]"]
  1k = Resistor [tolerance=±5% resistance=4.7k power=0.25W package=THT]
  LED3 = LED - 3mm [color="Blue (505nm)" current=0.030A package="3 mm [THT]"]
  j42 = female pin header, 4 pins [form="♀ (female)"]
  1uF = Electrolytic Capacitor [capacitance=1µF voltage=35V package="100 mil [THT, electrolytic]"]
  2N3907 = NPN-Transistor [package="TO92 [THT]"]
  10K = Resistor [tolerance=±5% resistance=10k power=0.25W package=THT]
  1K_4 = Resistor [tolerance=±5% resistance=1k power=0.25W package=THT]
  2N3908 = NPN-Transistor [package="TO92 [THT]"]
  10K_2 = Resistor [tolerance=±5% resistance=10k power=0.25W package=THT]
  1K_5 = Resistor [tolerance=±5% resistance=1k power=0.25W package=THT]
  1K_6 = Resistor [tolerance=±5% resistance=1k power=0.25W package=THT]
  LED2 = LED - 3mm [color="Blue (505nm)" current=0.030A package="3 mm [THT]"]
  2N3909 = NPN-Transistor [package="TO92 [THT]"]
  10K_3 = Resistor [tolerance=±5% resistance=10k power=0.25W package=THT]
  1K_7 = Resistor [tolerance=±5% resistance=1k power=0.25W package=THT]
  1K_8 = Resistor [tolerance=±5% resistance=1k power=0.25W package=THT]
  LED1 = LED - 3mm [color="Blue (505nm)" current=0.030A package="3 mm [THT]"]
  S10 = SPST Switch [package=switch-spdt_kit]
  1u = Electrolytic Capacitor [capacitance=1µF voltage=35V package="100 mil [THT, electrolytic]"]
  PT2399 = IC, DIP package, 16 pins [chip_label=IC]
  47u_2 = Electrolytic Capacitor [capacitance=47µF voltage=35V package="100 mil [THT, electrolytic]"]
  104 = Ceramic Capacitor [capacitance=100nF voltage=16V package="200 mil [THT, multilayer]"]
  104_2 = Ceramic Capacitor [capacitance=100nF voltage=16V package="200 mil [THT, multilayer]"]
  D1 = Schottky Diode [part_number=1N5817 package="300 mil [THT]"]
  L78L05 = NPN-Transistor [package="TO92 [THT]"]
  104_3 = Ceramic Capacitor [capacitance=100nF voltage=16V package="200 mil [THT, multilayer]"]
  104_4 = Ceramic Capacitor [capacitance=100nF voltage=16V package="200 mil [THT, multilayer]"]
  102 = Ceramic Capacitor [capacitance=1nF voltage=16V package="200 mil [THT, multilayer]"]
  102_2 = Ceramic Capacitor [capacitance=1nF voltage=16V package="200 mil [THT, multilayer]"]
  cm = female pin header, 4 pins [form="♀ (female)"]
  22k = Resistor [tolerance=±5% resistance=22k power=0.25W package=THT]
  10k = Resistor [tolerance=±5% resistance=10k power=0.25W package=THT]
  22k_2 = Resistor [tolerance=±5% resistance=22k power=0.25W package=THT]
  10k_2 = Resistor [tolerance=±5% resistance=22k power=0.25W package=THT]
  22k_3 = Resistor [tolerance=±5% resistance=22k power=0.25W package=THT]
  LED4 = LED - 3mm [color="Blue (505nm)" current=0.030A package="3 mm [THT]"]
  330 = Resistor [tolerance=±5% resistance=330 power=0.25W package=THT]
  LDR = Photocell (LDR) [power=0.25W dark_resistance_@0.01lx=300kΩ light_resistance_@100lx=400Ω luminance=10lx package=THT]
  Jamp8 = female pin header, 2 pins [form="♀ (female)"]
  Jx1 = female pin header, 3 pins [form="♀ (female)"]
  Jx2 = female pin header, 3 pins [form="♀ (female)"]
  Jamp7 = female pin header, 2 pins [form="♀ (female)"]
  Jamp9 = female pin header, 1 pin [form="♀ (female)"]

nets:
  N1: 100Kfm2.leg1, 1k.Pin_0, 2N3907.B, Jx2.pin1, Jx2.pin2, Jx2.pin3
  N2: 100Kfm2.wiper, LDR.pin_1
  N3: 100Kfm2.leg2, Jamp9.pin1
  N4: 4040A.Q13, j40.pin1
  N5: 4040A.Q14, j40.pin2
  N6: 4040A.Q6, j40.pin3
  N7: 4040A.Q5, j40.pin4
  N8: 4040A.Q7, j40.pin5
  N9: 4040A.Q4, j40.pin6
  GND: 4040A.Vss, 4040A.Reset, XR2206.GND, 100K.leg1, 100Kfm1.leg2, 4_7k_3.Pin_0, 1kshape.wiper, TRS1.Sleeve, Power_plug1.GND, out.pin2, 100K_2.leg2, LM324.VCC-, 47u.-, LED3.cathode, 2N3907.C, 2N3908.C, LED2.cathode, 2N3909.C, LED1.cathode, 1u.-, PT2399.pin3, PT2399.pin4, 47u_2.-, 104.1, 104_2.1, L78L05.B, LED4.cathode
  N10: 4040A.Q1, Jamp7.pin1, Jamp7.pin2
  N11: 4040A.Input_signal, LM324.2OUT, 100K_4.Pin_1, 1K_5.Pin_1, 330.Pin_1
  N12: 4040A.Q9, j42.pin4
  N13: 4040A.Q8, j42.pin3
  N14: 4040A.Q10, j42.pin2
  N15: 4040A.Q11, j42.pin1
  9V: 4040A.Vdd, XR2206.VCC, 4_7k_4.Pin_0, Power_plug1.VCC, LM324.VCC+, 10K.Pin_0, 10K_2.Pin_0, 10K_3.Pin_1, D1.anode
  N16: XR2206.AMSI, Jamp8.pin1, Jamp8.pin2
  N17: XR2206.STO, 1uf.-
  N18: XR2206.MO, 4_7k3.Pin_1
  N19: XR2206.TC1, 68nf.0
  N20: XR2206.TC2, 68nf.1
  N21: XR2206.TR1, 4_7k_2.Pin_0
  N22: XR2206.TR2, 4_7k.Pin_0
  N23: XR2206.FSKI, A/B.pin1, A/B.pin2
  N24: XR2206.SYNCO, 1u.+
  N25: XR2206.WAVEA1, 220.Pin_1
  N26: XR2206.WAVEA2, 220.Pin_0
  N27: XR2206.SYMA1, 1kshape.leg2
  N28: XR2206.SYMA2, 1kshape.leg1
  N29: 100K.wiper, 100K.leg2, PT2399.pin6
  N30: 4_7k.Pin_1, 100Kfm1.wiper
  N31: 1uf.+, 100K_2.leg1, 22k.Pin_1, 10k.Pin_1
  N32: 4_7k_2.Pin_1, LDR.pin_0
  N33: 100Kfm1.leg1, S10.P, Jx1.pin1, Jx1.pin2, Jx1.pin3
  N34: 4_7k_3.Pin_1, 4_7k_4.Pin_1, 4_7k3.Pin_0
  N35: 100Kamp.leg1, PT2399.pin15, 102_2.1, 22k.Pin_0
  N36: 100Kamp.wiper, TRS1.Ring, TRS1.Tip, out.pin1, 100K_2.wiper
  N37: 100Kamp.leg2, PT2399.pin14, 102.0, 22k_2.Pin_0
  N38: LM324.1OUT, 100K_5.Pin_0, 1uF.-, 1K_8.Pin_1, S10.S
  N39: LM324.1IN-, Jamp5.pin1
  N40: LM324.1IN+, 100K_5.Pin_1, 1K_3.Pin_0
  N41: LM324.2IN+, 100K_4.Pin_0, 1K_2.Pin_1
  N42: LM324.2IN-, Jamp4.pin1
  N43: LM324.3OUT, 100K_3.Pin_0, 1k.Pin_1
  N44: LM324.3IN-, Jamp1.pin1
  N45: LM324.3IN+, 100K_3.Pin_1, 1K.Pin_1
  N46: 1K.Pin_0, Jamp2.pin1, Jamp2.pin2
  N47: 1K_2.Pin_0, Jamp3.pin1, Jamp3.pin2
  N48: 1K_3.Pin_1, Jamp6.pin1, Jamp6.pin2
  N49: 47u.+, PT2399.pin2
  N50: LED3.anode, 1K_4.Pin_0
  N51: 1uF.+, S10.O
  N52: 2N3907.E, 10K.Pin_1, 1K_4.Pin_1
  N53: 2N3908.E, 10K_2.Pin_1, 1K_6.Pin_1
  N54: 2N3908.B, 1K_5.Pin_0
  N55: 1K_6.Pin_0, LED2.anode
  N56: 2N3909.E, 10K_3.Pin_0, 1K_7.Pin_1
  N57: 2N3909.B, 1K_8.Pin_0
  N58: 1K_7.Pin_0, LED1.anode
  N59: PT2399.pin1, 47u_2.+, L78L05.E
  N60: PT2399.pin7, 104_2.0
  N61: PT2399.pin8, 104.0
  N62: PT2399.pin9, 104_3.1
  N63: PT2399.pin10, 104_3.0
  N64: PT2399.pin11, 104_4.1
  N65: PT2399.pin12, 104_4.0, 22k_3.Pin_0
  N66: PT2399.pin13, 102.1, 10k_2.Pin_0
  N67: PT2399.pin16, 102_2.0, 10k.Pin_0
  N68: D1.cathode, L78L05.C
  N69: cm.pin1, cm.pin2, cm.pin3, cm.pin4
  N70: 22k_2.Pin_1, 10k_2.Pin_1, 22k_3.Pin_1
  N71: LED4.anode, 330.Pin_0

notes:
  moat
  shark
  blueprint@poetaster.de 2025   jlclcjlcjlcjlc

custom parts:
  CD4040E: CD4020B, CD4024B, and CD4040B are ripple-carry binary counters. All counter stages are master-slave flip-flops. The state of a counter advances one count on the negative transition of each input pulse; a high level on the RESET line resets the counter to its all zeros state. Schmitt trigger action on the input-pulse line permits unlimited rise and fall times. All inputs and outputs are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
