# Fritzing sketch moat (saved by Fritzing 1.0.2b)
circuit board: 4.99999cm x 10cm
breadboards: 2

parts:
  100Kfm2 = Rotary Potentiometer (Small) [maximum_resistance=100kΩ knob_status=50% power=0.5W package=THT]
  4040A = CD4040E [package="DIP16 [THT]"]
  XR2206 = XR2206 [package=dil16]
  100Ks1 = Rotary Potentiometer (Small) [maximum_resistance=100kΩ knob_status=50% power=0.5W package=THT]
  j40 = female pin header, 6 pins [form="♀ (female)"]
  4_7k = Resistor [tolerance=±5% resistance=4.7k power=0.25W package=THT]
  Jx1 = female pin header, 2 pins [form="♀ (female)"]
  A/B = female pin header, 2 pins [form="♀ (female)"]
  Jx2 = female pin header, 2 pins [form="♀ (female)"]
  1uf = Electrolytic Capacitor [capacitance=1µF voltage=16V package="100 mil [THT, electrolytic]"]
  4_7k_2 = Resistor [tolerance=±5% resistance=4.7k power=0.25W package=THT]
  68nf = Ceramic Capacitor [capacitance=68nF voltage=16V package="200 mil [THT, multilayer]"]
  220o = Resistor [tolerance=±5% resistance=220 power=0.25W package=THT]
  Jm1 = female pin header, 3 pins [form="♀ (female)"]
  100Kfm1 = Rotary Potentiometer (Small) [maximum_resistance=100kΩ knob_status=50% power=0.5W package=THT]
  4_7k_3 = Resistor [tolerance=±1% resistance=4.7k power=0.25W package=THT]
  4_7k_4 = Resistor [tolerance=±1% resistance=4.7k power=0.25W package=THT]
  100Kamp = Rotary Potentiometer (Small) [maximum_resistance=100kΩ knob_status=50% power=0.5W package=THT]
  1kshape = Rotary Potentiometer (Small) [maximum_resistance=1kΩ knob_status=50% power=0.5W package=THT]
  4_7k3 = Resistor [tolerance=±5% resistance=4.7k power=0.25W package=THT]
  TRS1 = Audio Jack (TRS) 3.5mm [package="PG203J [THT]"]
  Power_plug1 = Power plug
  out = female pin header, 2 pins [form="♀ (female)"]
  100Ks2 = Rotary Potentiometer (Small) [maximum_resistance=100kΩ knob_status=50% power=0.5W package=THT]
  Jm2 = female pin header, 3 pins [form="♀ (female)"]
  LM324 = LM124-324 Quad Opamp [package="DIP (Dual Inline)"]
  100K = Resistor [tolerance=±5% resistance=100k power=0.25W package=THT]
  1K = Resistor [tolerance=±5% resistance=1k power=0.25W package=THT]
  100K_2 = Resistor [tolerance=±5% resistance=100k power=0.25W package=THT]
  1K_2 = Resistor [tolerance=±5% resistance=1k power=0.25W package=THT]
  100K_3 = Resistor [tolerance=±5% resistance=100k power=0.25W package=THT]
  1K_3 = Resistor [tolerance=±5% resistance=1k power=0.25W package=THT]
  4040B = CD4040E [package="DIP16 [THT]"]
  j41 = female pin header, 6 pins [form="♀ (female)"]
  opcom = female pin header, 4 pins [form="♀ (female)"]
  Jamp5 = female pin header, 1 pin [form="♀ (female)"]
  Jamp4 = female pin header, 1 pin [form="♀ (female)"]
  Jamp1 = female pin header, 1 pin [form="♀ (female)"]
  Jamp2 = female pin header, 2 pins [form="♀ (female)"]
  Jamp3 = female pin header, 2 pins [form="♀ (female)"]
  Jamp6 = female pin header, 2 pins [form="♀ (female)"]
  47uF = Electrolytic Capacitor [capacitance=47µF voltage=35V package="100 mil [THT, electrolytic]"]
  4_7k4 = Resistor [tolerance=±5% resistance=4.7k power=0.25W package=THT]
  LED3 = LED - 3mm [color="Blue (505nm)" current=0.030A package="3 mm [THT]"]
  j42 = female pin header, 4 pins [form="♀ (female)"]
  1uF = Electrolytic Capacitor [capacitance=1µF voltage=35V package="100 mil [THT, electrolytic]"]
  2N3907 = NPN-Transistor [package="TO92 [THT]"]
  10K = Resistor [tolerance=±5% resistance=10k power=0.25W package=THT]
  1K1 = Resistor [tolerance=±5% resistance=1k power=0.25W package=THT]
  1K2 = Resistor [tolerance=±5% resistance=1k power=0.25W package=THT]
  2N3908 = NPN-Transistor [package="TO92 [THT]"]
  10K1 = Resistor [tolerance=±5% resistance=10k power=0.25W package=THT]
  1K3 = Resistor [tolerance=±5% resistance=1k power=0.25W package=THT]
  1K4 = Resistor [tolerance=±5% resistance=1k power=0.25W package=THT]
  LED2 = LED - 3mm [color="Blue (505nm)" current=0.030A package="3 mm [THT]"]
  2N3909 = NPN-Transistor [package="TO92 [THT]"]
  10K2 = Resistor [tolerance=±5% resistance=10k power=0.25W package=THT]
  1K5 = Resistor [tolerance=±5% resistance=1k power=0.25W package=THT]
  1K6 = Resistor [tolerance=±5% resistance=1k power=0.25W package=THT]
  LED1 = LED - 3mm [color="Blue (505nm)" current=0.030A package="3 mm [THT]"]
  S10 = SPST Switch [package=switch-spdt_kit]
  amOut = female pin header, 2 pins [form="♀ (female)"]
  47u = Electrolytic Capacitor [capacitance=1µF voltage=35V package="100 mil [THT, electrolytic]"]

nets:
  N1: 100Kfm2.leg1, Jx2.pin1, Jx2.pin2, 100Ks2.wiper, Jm2.pin2
  N2: 100Kfm2.wiper, 4_7k.Pin_1
  N3: 100Kfm2.leg2, 100Kfm1.leg2, S10.S
  N4: 4040A.Q13, j40.pin1
  N5: 4040A.Q14, j40.pin2
  N6: 4040A.Q6, j40.pin3
  N7: 4040A.Q5, j40.pin4
  N8: 4040A.Q7, j40.pin5
  N9: 4040A.Q4, j40.pin6
  GND: 4040A.Vss, 4040A.Reset, XR2206.GND, 4_7k_3.Pin_0, 100Kamp.leg1, 1kshape.wiper, TRS1.Sleeve, Power_plug1.GND, out.pin1, LM324.VCC-, 4040B.Vss, 4040B.Reset, 47uF.-, LED3.cathode, 1uF.-, 2N3907.C, 2N3908.C, LED2.cathode, 2N3909.C, LED1.cathode, S10.P, 47u.-
  N10: 4040A.Q1, 100Ks1.leg2, Jm1.pin1
  N11: 4040A.Input_signal, LM324.2OUT, 100K_2.Pin_1, 1K3.Pin_1
  N12: 4040A.Q9, j42.pin4
  N13: 4040A.Q8, j42.pin3
  N14: 4040A.Q10, j42.pin2
  N15: 4040A.Q11, j42.pin1
  9V: 4040A.Vdd, XR2206.VCC, 4_7k_4.Pin_0, Power_plug1.VCC, LM324.VCC+, 4040B.Vdd, 10K.Pin_0, 10K1.Pin_0, 10K2.Pin_1
  N16: XR2206.AMSI, 100Kamp.wiper, 47uF.+, 1uF.+, amOut.pin1, amOut.pin2
  N17: XR2206.STO, 1uf.-
  N18: XR2206.MO, 4_7k3.Pin_1
  N19: XR2206.TC1, 68nf.0
  N20: XR2206.TC2, 68nf.1
  N21: XR2206.TR1, 4_7k_2.Pin_0
  N22: XR2206.TR2, 4_7k.Pin_0
  N23: XR2206.FSKI, A/B.pin1, A/B.pin2
  N24: XR2206.SYNCO, 47u.+
  N25: XR2206.WAVEA1, 220o.Pin_1
  N26: XR2206.WAVEA2, 220o.Pin_0
  N27: XR2206.SYMA1, 1kshape.leg2
  N28: XR2206.SYMA2, 1kshape.leg1
  N29: 100Ks1.leg1, Jm1.pin3
  N30: 100Ks1.wiper, Jx1.pin1, Jx1.pin2, Jm1.pin2, 100Kfm1.leg1
  N31: 1uf.+, TRS1.Ring, TRS1.Tip, out.pin2
  N32: 4_7k_2.Pin_1, 100Kfm1.wiper
  N33: 4_7k_3.Pin_1, 4_7k_4.Pin_1, 4_7k3.Pin_0
  N34: 100Kamp.leg2, 4_7k4.Pin_0, 1K2.Pin_1
  N35: 100Ks2.leg1, Jm2.pin3
  N36: 100Ks2.leg2, Jm2.pin1, 4040B.Q1
  N37: LM324.1OUT, 100K_3.Pin_0, 4040B.Input_signal, 1K6.Pin_1
  N38: LM324.1IN-, Jamp5.pin1
  N39: LM324.1IN+, 100K_3.Pin_1, 1K_3.Pin_0
  N40: LM324.2IN+, 100K_2.Pin_0, 1K_2.Pin_1
  N41: LM324.2IN-, Jamp4.pin1
  N42: LM324.3OUT, 100K.Pin_0, 4_7k4.Pin_1
  N43: LM324.3IN-, Jamp1.pin1
  N44: LM324.3IN+, 100K.Pin_1, 1K.Pin_1
  N45: 1K.Pin_0, Jamp2.pin1, Jamp2.pin2
  N46: 1K_2.Pin_0, Jamp3.pin1, Jamp3.pin2
  N47: 1K_3.Pin_1, Jamp6.pin1, Jamp6.pin2
  N48: 4040B.Q13, j41.pin1
  N49: 4040B.Q14, j41.pin2
  N50: 4040B.Q6, j41.pin3
  N51: 4040B.Q5, j41.pin4
  N52: 4040B.Q7, j41.pin5
  N53: 4040B.Q4, j41.pin6
  N54: opcom.pin1, opcom.pin2, opcom.pin3, opcom.pin4
  N55: LED3.anode, 1K1.Pin_0
  N56: 2N3907.E, 10K.Pin_1, 1K1.Pin_1
  N57: 2N3907.B, 1K2.Pin_0
  N58: 2N3908.E, 10K1.Pin_1, 1K4.Pin_1
  N59: 2N3908.B, 1K3.Pin_0
  N60: 1K4.Pin_0, LED2.anode
  N61: 2N3909.E, 10K2.Pin_0, 1K5.Pin_1
  N62: 2N3909.B, 1K6.Pin_0
  N63: 1K5.Pin_0, LED1.anode

notes:
  moat
  blueprint@poetaster.de 2024

custom parts:
  CD4040E: CD4020B, CD4024B, and CD4040B are ripple-carry binary counters. All counter stages are master-slave flip-flops. The state of a counter advances one count on the negative transition of each input pulse; a high level on the RESET line resets the counter to its all zeros state. Schmitt trigger action on the input-pulse line permits unlimited rise and fall times. All inputs and outputs are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
