# Fritzing sketch moat.v1 (saved by Fritzing 0.9.3b)
circuit board: 8.4cm x 5.5cm
breadboards: 1

parts:
  R1 = Rotary Potentiometer (Small) [maximum_resistance=100kΩ package=THT]
  R5 = Rotary Potentiometer (Small) [maximum_resistance=100kΩ package=THT]
  R7 = Rotary Potentiometer (Small) [maximum_resistance=100kΩ package=THT]
  R9 = Rotary Potentiometer (Small) [maximum_resistance=100kΩ package=THT]
  4040 = CD4040E [package="DIP16 [THT]"]
  XR = XR2206 [package=dil16]
  R2 = Rotary Potentiometer (Small) [maximum_resistance=100kΩ package=THT]
  R6 = Rotary Potentiometer (Small) [maximum_resistance=100kΩ package=THT]
  C1 = Electrolytic Capacitor [capacitance=1µF voltage=16V package="100 mil [THT, electrolytic]"]
  R4 = Rotary Potentiometer (Small) [maximum_resistance=100kΩ package=THT]
  J1 = female pin header, 3 pins [form="♀ (female)"]
  J4 = female pin header, 3 pins [form="♀ (female)"]
  40106 = IC, DIP package, 14 pins [chip_label=40106 spacing=300mil]
  TRS1 = Audio Jack (TRS) 3.5mm [package="PG203J [THT]"]
  J3 = female pin header, 4 pins [form="♀ (female)"]
  R3 = Rotary Potentiometer (Small) [maximum_resistance=10kΩ package=THT]
  C3 = Ceramic Capacitor [capacitance=47nF voltage=16V package="200 mil [THT, multilayer]"]
  R12 = Resistor [tolerance=±5% resistance=330 package=THT]
  LED2 = LED - 3mm [color="White (8000K)" package="3 mm [THT]"]
  J2 = female pin header, 6 pins [form="♀ (female)"]
  D2 = Rectifier Diode [part_number=1N4001 package="300 mil [THT]"]
  J9 = female pin header, 2 pins [form="♀ (female)"]
  J10 = female pin header, 2 pins [form="♀ (female)"]
  R16 = Resistor [tolerance=±5% resistance=4.7k package=THT]
  J11 = female pin header, 2 pins [form="♀ (female)"]
  J6 = female pin header, 3 pins [form="♀ (female)"]
  J7 = female pin header, 3 pins [form="♀ (female)"]
  J8 = female pin header, 3 pins [form="♀ (female)"]
  J13 = female pin header, 2 pins [form="♀ (female)"]
  J14 = female pin header, 2 pins [form="♀ (female)"]
  J15 = female pin header, 2 pins [form="♀ (female)"]
  R17 = Resistor [tolerance=±5% resistance=4.7k package=THT]
  C10 = Electrolytic Capacitor [capacitance=10µF voltage=16V package="100 mil [THT, electrolytic]"]
  C9 = Electrolytic Capacitor [capacitance=1µF voltage=16V package="100 mil [THT, electrolytic]"]
  C2 = Electrolytic Capacitor [capacitance=10μF voltage=16V package="100 mil [THT, electrolytic]"]
  R14 = Resistor [tolerance=±5% resistance=10k package=THT]
  R13 = Resistor [tolerance=±5% resistance=10k package=THT]
  J12 = female pin header, 2 pins [form="♀ (female)"]
  C7 = Electrolytic Capacitor [capacitance=1µF voltage=16V package="100 mil [THT, electrolytic]"]
  R15 = Resistor [tolerance=±5% resistance=4.7k package=THT]
  C6 = Ceramic Capacitor [capacitance=47nF voltage=16V package="200 mil [THT, multilayer]"]
  R18 = Resistor [tolerance=±5% resistance=330 package=THT]
  LED3 = LED - 3mm [color="White (8000K)" package="3 mm [THT]"]
  J16 = female pin header, 2 pins [form="♀ (female)"]
  R19 = Photocell (LDR) [package=THT]
  J2a = female pin header, 6 pins [form="♀ (female)"]
  J6a = female pin header, 3 pins [form="♀ (female)"]
  J6a1 = female pin header, 3 pins [form="♀ (female)"]
  J6a2 = female pin header, 3 pins [form="♀ (female)"]
  Power_plug1 = Power plug
  C11 = Ceramic Capacitor [capacitance=1nF voltage=16V package="200 mil [THT, multilayer]"]
  J17 = female pin header, 3 pins [form="♀ (female)"]
  R20 = Trimmer Potentiometer [maximum_resistance=20kΩ package=THT]
  R22 = Resistor [tolerance=±1% resistance=1k package=THT]
  R23 = Resistor [tolerance=±1% resistance=1k package=THT]
  R21 = Trimmer Potentiometer [maximum_resistance=20kΩ package=THT]

nets:
  N1: R1.wiper, 40106.pin5, C2.+
  N2: R1.leg2, 4040.Input_signal, 40106.pin6, J6.pin1, J6.pin2, J6.pin3, R18.Pin_0
  N3: R5.leg1, J4.pin1
  N4: R5.wiper, J4.pin2, J7.pin1, J7.pin2, J7.pin3, R14.Pin_1
  N5: R5.leg2, J4.pin3
  N6: R7.leg1, J12.pin1, J12.pin2
  N7: R7.wiper, R16.Pin_1
  GND: R7.leg2, 4040.Vss, XR.GND, R6.leg2, C1.-, 40106.pin7, TRS1.Sleeve, C3.1, LED2.cathode, J9.pin1, J9.pin2, C10.-, C9.-, C2.-, LED3.cathode, J16.pin1, R19.pin_1, Power_plug1.GND, C11.0, C11.1, J17.pin1, J17.pin2, J17.pin3, R20.wiper, R23.Pin_0
  N8: R9.leg1, R3.leg2, C3.0
  N9: R9.wiper, TRS1.Ring
  N10: R9.leg2, J15.pin1, J15.pin2, C7.+
  N11: 4040.Q13, J2.pin1, J2a.pin1
  N12: 4040.Q14, J2.pin2, J2a.pin2
  N13: 4040.Q6, J2.pin3, J2a.pin3
  N14: 4040.Q5, J2.pin4, J2a.pin4
  N15: 4040.Q7, J2.pin5, J2a.pin5
  N16: 4040.Q4, J2.pin6, J2a.pin6
  N17: 4040.Q1, J6a.pin1, J6a.pin2, J6a.pin3
  N18: 4040.Vdd, 40106.pin14, D2.cathode, J10.pin1, J10.pin2, R17.Pin_0, R22.Pin_0
  N19: XR.AMSI, J14.pin1, J14.pin2
  N20: XR.STO, C7.-
  N21: XR.MO, R21.leg2
  N22: XR.TC1, C6.0
  N23: XR.TC2, C6.1
  N24: XR.TR1, R15.Pin_0
  N25: XR.TR2, R16.Pin_0
  N26: XR.FSKI, J13.pin1, J13.pin2
  N27: XR.BIAS, C10.+
  N28: XR.SYNCO, R17.Pin_1
  N29: XR.SYMA1, R20.leg2
  N30: XR.SYMA2, R20.leg1
  N31: R2.wiper, C1.+, 40106.pin9, R14.Pin_0, R13.Pin_0
  N32: R2.leg2, 40106.pin8, R3.wiper, R12.Pin_0
  N33: R6.leg1, J11.pin1, J11.pin2
  N34: R6.wiper, R15.Pin_1
  N35: R4.leg1, J1.pin1
  N36: R4.wiper, J1.pin2, J8.pin1, J8.pin2, J8.pin3, R13.Pin_1
  N37: R4.leg2, J1.pin3
  N38: 40106.pin1, J6a1.pin1, J6a1.pin2, J6a1.pin3
  N39: 40106.pin2, J6a2.pin1, J6a2.pin2, J6a2.pin3
  N40: 40106.pin10, J3.pin4
  N41: 40106.pin11, J3.pin3
  N42: 40106.pin12, J3.pin2
  N43: 40106.pin13, J3.pin1
  N44: R3.leg1, C9.+
  N45: R12.Pin_1, LED2.anode
  N46: D2.anode, Power_plug1.VCC
  N47: R18.Pin_1, LED3.anode
  N48: J16.pin2, R19.pin_0
  N49: R22.Pin_1, R23.Pin_1, R21.leg1, R21.wiper

custom parts:
  CD4040E: CD4020B, CD4024B, and CD4040B are ripple-carry binary counters. All counter stages are master-slave flip-flops. The state of a counter advances one count on the negative transition of each input pulse; a high level on the RESET line resets the counter to its all zeros state. Schmitt trigger action on the input-pulse line permits unlimited rise and fall times. All inputs and outputs are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
